# Fritzing sketch ArduinoCircuit (saved by Fritzing 0.9.3b)
breadboards: 1

parts:
  Part1 = Arduino Uno (Rev3)
  T1 = LM35 Temperature Sensor [package="TO92 [THT]"]
  RHT1 = Humidity and Temperature Sensor RHT03
  R1 = Resistor [tolerance=±5% resistance=1k package=THT]
  R2 = PHOTOCELL [package=photocell-kit]
  R3 = Resistor [tolerance=±5% resistance=1k package=THT]
  hc-sr1 = hc-sr04
  LED1 = smd LED [color="Red (633nm)" package="1206 [SMD]"]
  R4 = Resistor [tolerance=±5% resistance=1k package=THT]
  J1 = Piezo Speaker
  R5 = Resistor [tolerance=±0.1% resistance=1k package=THT]
  Part2 = Bluetooth HC-05 Macho

nets:
  GND: Part1.A0, Part1.GND, T1.GND, RHT1.GND_2, R3.Pin_1, hc-sr1.GND, LED1.cathode, R5.Pin_1, Part2.GND
  N1: Part1.A1, T1.Vout
  N2: Part1.D10_PWM/SS, RHT1.Data-signal, R1.Pin_1
  N3: Part1.D11_PWM/MOSI, J1.pin2
  N4: Part1.D12/MISO, Part2.RXD
  N5: Part1.D13/SCK, Part2.TXD
  N6: Part1.D4, R4.Pin_0
  N7: Part1.D6_PWM, hc-sr1.Echo
  N8: Part1.D7, hc-sr1.Trig
  VCC: Part1.5V, T1.+Vs, RHT1.Vcc, R1.Pin_0, R2.P$1, hc-sr1.VCC, Part2.VCC
  N9: R2.P$2, R3.Pin_0
  N10: LED1.anode, R4.Pin_1
  N11: J1.pin1, R5.Pin_0
