# Fritzing sketch ArduinoCircuit (saved by Fritzing 0.9.3b)
breadboards: 2

parts:
  Part1 = Arduino Uno (Rev3)
  T1 = LM35 Temperature Sensor [package="TO92 [THT]"]
  RHT1 = Humidity and Temperature Sensor RHT03
  R1 = Resistor [tolerance=±5% resistance=1k package=THT]
  R2 = PHOTOCELL [package=photocell-kit]
  R3 = Resistor [tolerance=±5% resistance=1k package=THT]
  hc-sr1 = hc-sr04
  LED1 = smd LED [color="Red (633nm)" package="1206 [SMD]"]
  R4 = Resistor [tolerance=±5% resistance=1k package=THT]
  J1 = Basic Servo
  LCD2 = LCD screen
  R5 = Rotary Potentiometer (Large) [maximum_resistance=10kΩ package=THT]
  R6 = Resistor [tolerance=±5% resistance=220 package="0603 [SMD]"]
  J2 = Piezo Speaker

nets (from the schematic view):
  GND: Part1.A0, Part1.GND, T1.GND, RHT1.GND_2, R3.Pin_1, hc-sr1.GND, LED1.cathode, J1.gnd, LCD2.VSS, LCD2.R/W, LCD2.LED-, R5.leg1, J2.pin1
  N1: Part1.A1, T1.Vout
  N2: Part1.A2, LCD2.DB7
  N3: Part1.A3, LCD2.DB6
  N4: Part1.A4/SDA, LCD2.DB5
  N5: Part1.A5/SCL, LCD2.DB4
  N6: Part1.D9_PWM, J2.pin2
  N7: Part1.D10_PWM/SS, RHT1.Data-signal, R1.Pin_1
  N8: Part1.D2, J1.pulse
  N9: Part1.D3_PWM, LCD2.E
  N10: Part1.D4, R4.Pin_0
  N11: Part1.D5_PWM, LCD2.RS
  N12: Part1.D6_PWM, hc-sr1.Echo
  N13: Part1.D7, hc-sr1.Trig
  VCC: Part1.5V, T1.+Vs, RHT1.Vcc, R1.Pin_0, R2.P$1, hc-sr1.VCC, J1.vcc, LCD2.VDD, R5.leg2, R6.Pin_0
  N14: R2.P$2, R3.Pin_0
  N15: LED1.anode, R4.Pin_1
  N16: LCD2.V0, R5.wiper
  N17: LCD2.LED+, R6.Pin_1
